# Fritzing sketch breadboard (saved by Fritzing 0.8.7b)
breadboards: 1

parts:
  Part1 = Arduino Mega 2560 (Rev3)
  NEOPIXEL1 = Neopixel Strip -- White (60/m)
  C1 = Capacitor Polarized [package=cpol-radial-1000uf-25v]
  R1 = Resistor [tolerance=±5% resistance=330 package=THT]
  JACK1 = 2.1mm Barrel Jack with Terminal Block

nets:
  GND: Part1.GND, NEOPIXEL1.GND, C1.-, JACK1.NEG
  VIN: Part1.VIN, NEOPIXEL1.+5V, C1.+, JACK1.POS
  N1: Part1.D6_PWM, R1.Pin_1
  N2: NEOPIXEL1.DI, R1.Pin_0

notes:
  5V/10A power supply for large LED strip

custom parts:
  Neopixel Strip -- White (60/m): Neopixel Strip, White, 60 pixels per meter.
